// Logisim project 2 bit adder with NAND.circ as structural Verilog: 1 circuit, main circuit main
module main (
  input  A,
  input  B,
  output S,
  output C
);

  wire nand_1_out, nand_2_out, nand_3_out, undriven;

  nand nand_1 (nand_1_out, A, B);
  nand nand_2 (nand_2_out, A, undriven);
  nand nand_3 (nand_3_out, undriven, B);
  nand nand_4 (S, nand_2_out, nand_3_out);
  nand nand_5 (C, nand_1_out, nand_1_out);
endmodule
