// Logisim project 3 bit full adder.circ as structural Verilog: 1 circuit, main circuit main
module main (
  input  in_1,
  input  in_2,
  input  in_3,
  output out_4,
  output out_5
);

  wire and_1_out, and_2_out, undriven;

  xor xor_1 (in_3, in_1, in_2);
  xor xor_2 (out_4, in_3, undriven);
  and and_1 (and_1_out, undriven, in_3);
  and and_2 (and_2_out, in_1, in_2);
  or or_1 (out_5, and_1_out, and_2_out);
endmodule
